# Fritzing sketch Theremin5x5 (saved by Fritzing 0.9.6b)
breadboards: 2

parts:
  Part1 = Arduino Mega 2560 (Rev3)
  HC-SR04_Sensor_1 = HC-SR04 Ultrasonic Distance Sensor
  HC-SR04_Sensor_2 = HC-SR04 Ultrasonic Distance Sensor
  HC-SR04_Sensor_3 = HC-SR04 Ultrasonic Distance Sensor
  HC-SR04_Sensor_4 = HC-SR04 Ultrasonic Distance Sensor
  HC-SR04_Sensor_5 = HC-SR04 Ultrasonic Distance Sensor
  LED1 = smd LED [color="Red (633nm)" package="0805 [SMD]"]
  LED2 = smd LED [color="Red (633nm)" package="0805 [SMD]"]
  LED3 = smd LED [color="Red (633nm)" package="0805 [SMD]"]
  LED4 = smd LED [color="Red (633nm)" package="0805 [SMD]"]
  LED5 = smd LED [color="Red (633nm)" package="0805 [SMD]"]
  R1 = Resistor [tolerance=±5% power=0.25 resistance=100 package=THT]
  R2 = Resistor [tolerance=±5% power=0.25 resistance=100 package=THT]
  R3 = Resistor [tolerance=±5% power=0.25 resistance=100 package=THT]
  R4 = Resistor [tolerance=±5% power=0.25 resistance=100 package=THT]
  R5 = Resistor [tolerance=±5% power=0.25 resistance=100 package=THT]
  S1 = Pushbutton [package="[THT]"]
  R6 = Resistor [tolerance=±5% power=0.25 resistance=10k package=THT]
  LED6 = smd LED [color="Green (560nm)" package="0805 [SMD]"]
  R7 = Resistor [tolerance=±5% power=0.25 resistance=100 package=THT]
  R8 = Resistor [tolerance=±5% power=0.25 resistance=100 package=THT]
  R9 = Resistor [tolerance=±5% power=0.25 resistance=100 package=THT]
  R10 = Resistor [tolerance=±5% power=0.25 resistance=100 package=THT]
  R11 = Resistor [tolerance=±5% power=0.25 resistance=100 package=THT]
  LED7 = smd LED [color="Green (560nm)" package="0805 [SMD]"]
  LED8 = smd LED [color="Green (560nm)" package="0805 [SMD]"]
  LED9 = smd LED [color="Green (560nm)" package="0805 [SMD]"]
  LED10 = smd LED [color="Green (560nm)" package="0805 [SMD]"]

nets:
  N1: Part1.D13_PWM, S1.Pin_1, S1.Pin_2, R6.Pin_0
  VCC: Part1.5V, HC-SR04_Sensor_1.VCC, HC-SR04_Sensor_2.VCC, HC-SR04_Sensor_3.VCC, HC-SR04_Sensor_4.VCC, HC-SR04_Sensor_5.VCC, S1.Pin_3, S1.Pin_4
  GND: Part1.GND, HC-SR04_Sensor_1.GND, HC-SR04_Sensor_2.GND, HC-SR04_Sensor_3.GND, HC-SR04_Sensor_4.GND, HC-SR04_Sensor_5.GND, R1.Pin_0, R2.Pin_0, R3.Pin_0, R4.Pin_0, R5.Pin_0, R6.Pin_1, R7.Pin_1, R8.Pin_1, R9.Pin_1, R10.Pin_1, R11.Pin_1
  N2: Part1.D2_PWM, LED10.anode
  N3: Part1.D3_PWM, LED9.anode
  N4: Part1.D4_PWM, LED8.anode
  N5: Part1.D5_PWM, LED7.anode
  N6: Part1.D6_PWM, LED6.anode
  N7: Part1.D22, LED1.anode
  N8: Part1.D24, LED2.anode
  N9: Part1.D26, LED3.anode
  N10: Part1.D28, LED4.anode
  N11: Part1.D30, LED5.anode
  N12: Part1.D44, HC-SR04_Sensor_2.TRIG
  N13: Part1.D45, HC-SR04_Sensor_2.ECHO
  N14: Part1.D46, HC-SR04_Sensor_1.TRIG
  N15: Part1.D47, HC-SR04_Sensor_1.ECHO
  N16: Part1.D48, HC-SR04_Sensor_3.TRIG
  N17: Part1.D49, HC-SR04_Sensor_3.ECHO
  N18: Part1.D50, HC-SR04_Sensor_4.TRIG
  N19: Part1.D51, HC-SR04_Sensor_4.ECHO
  N20: Part1.D52, HC-SR04_Sensor_5.TRIG
  N21: Part1.D53, HC-SR04_Sensor_5.ECHO
  N22: LED1.cathode, R2.Pin_1
  N23: LED2.cathode, R4.Pin_1
  N24: LED3.cathode, R3.Pin_1
  N25: LED4.cathode, R1.Pin_1
  N26: LED5.cathode, R5.Pin_1
  N27: LED6.cathode, R7.Pin_0
  N28: R8.Pin_0, LED7.cathode
  N29: R9.Pin_0, LED8.cathode
  N30: R10.Pin_0, LED9.cathode
  N31: R11.Pin_0, LED10.cathode
